// Logisim project comparator Logisim.circ as structural Verilog: 3 circuits, main circuit EQ metr XORs en OR
module EQ_metr_XORs_en_OR (
  input  A2,
  input  B2,
  input  A1,
  input  B1,
  input  A0,
  input  B0,
  output EQ
);

  wire A0_xor_B0, A1_xor_B1, A2_xor_B2, nA0, nA1, nA2, nB0, nB1, nB2, transistor_15_out, transistor_18_out,
       transistor_19_out, transistor_22_out, transistor_23_out, transistor_26_out, transistor_27_out,
       transistor_30_out, transistor_31_out, transistor_34_out, transistor_35_out, transistor_38_out,
       transistor_40_out, transistor_41_out;

  Transistor transistor_1 ();  // open: in, out, gate
  Transistor transistor_2 (.in(1'b1), .out(nA2), .gate(A2));
  Transistor #(.\type ("n")) transistor_3 (.in(1'b0), .out(nA2), .gate(A2));
  Transistor transistor_4 (.in(1'b1), .out(nA1), .gate(A1));
  Transistor #(.\type ("n")) transistor_5 (.in(1'b0), .out(nA1), .gate(A1));
  Transistor transistor_6 (.in(1'b1), .out(nA0), .gate(A0));
  Transistor #(.\type ("n")) transistor_7 (.in(1'b0), .out(nA0), .gate(A0));
  Transistor #(.\type ("n")) transistor_8 ();  // open: in, out, gate
  Transistor transistor_9 (.in(1'b1), .out(nB2), .gate(B2));
  Transistor #(.\type ("n")) transistor_10 (.in(1'b0), .out(nB2), .gate(B2));
  Transistor transistor_11 (.in(1'b1), .out(nB1), .gate(B1));
  Transistor #(.\type ("n")) transistor_12 (.in(1'b0), .out(nB1), .gate(B1));
  Transistor transistor_13 (.in(1'b1), .out(nB0), .gate(B0));
  Transistor #(.\type ("n")) transistor_14 (.in(1'b0), .out(nB0), .gate(B0));
  Transistor transistor_15 (.in(1'b1), .out(transistor_15_out), .gate(A2));
  Transistor transistor_16 (.in(transistor_15_out), .out(A2_xor_B2), .gate(nB2));
  Transistor #(.\type ("n")) transistor_17 (.in(transistor_18_out), .out(A2_xor_B2), .gate(A2));
  Transistor #(.\type ("n")) transistor_18 (.in(1'b0), .out(transistor_18_out), .gate(B2));
  Transistor transistor_19 (.in(1'b1), .out(transistor_19_out), .gate(nA2));
  Transistor transistor_20 (.in(transistor_19_out), .out(A2_xor_B2), .gate(B2));
  Transistor #(.\type ("n")) transistor_21 (.in(transistor_22_out), .out(A2_xor_B2), .gate(nA2));
  Transistor #(.\type ("n")) transistor_22 (.in(1'b0), .out(transistor_22_out), .gate(nB2));
  Transistor transistor_23 (.in(1'b1), .out(transistor_23_out), .gate(A1));
  Transistor transistor_24 (.in(transistor_23_out), .out(A1_xor_B1), .gate(nB1));
  Transistor #(.\type ("n")) transistor_25 (.in(transistor_26_out), .out(A1_xor_B1), .gate(A1));
  Transistor #(.\type ("n")) transistor_26 (.in(1'b0), .out(transistor_26_out), .gate(B1));
  Transistor transistor_27 (.in(1'b1), .out(transistor_27_out), .gate(nA1));
  Transistor transistor_28 (.in(transistor_27_out), .out(A1_xor_B1), .gate(B1));
  Transistor #(.\type ("n")) transistor_29 (.in(transistor_30_out), .out(A1_xor_B1), .gate(nA1));
  Transistor #(.\type ("n")) transistor_30 (.in(1'b0), .out(transistor_30_out), .gate(nB1));
  Transistor transistor_31 (.in(1'b1), .out(transistor_31_out), .gate(A0));
  Transistor transistor_32 (.in(transistor_31_out), .out(A0_xor_B0), .gate(nB0));
  Transistor #(.\type ("n")) transistor_33 (.in(transistor_34_out), .out(A0_xor_B0), .gate(A0));
  Transistor #(.\type ("n")) transistor_34 (.in(1'b0), .out(transistor_34_out), .gate(B0));
  Transistor transistor_35 (.in(1'b1), .out(transistor_35_out), .gate(nA0));
  Transistor transistor_36 (.in(transistor_35_out), .out(A0_xor_B0), .gate(B0));
  Transistor #(.\type ("n")) transistor_37 (.in(transistor_38_out), .out(A0_xor_B0), .gate(nA0));
  Transistor #(.\type ("n")) transistor_38 (.in(1'b0), .out(transistor_38_out), .gate(nB0));
  Transistor #(.\type ("n")) transistor_39 (.in(1'b0), .out(EQ), .gate(A2_xor_B2));
  Transistor transistor_40 (.in(1'b1), .out(transistor_40_out), .gate(A2_xor_B2));
  Transistor transistor_41 (.in(transistor_40_out), .out(transistor_41_out), .gate(A1_xor_B1));
  Transistor transistor_42 (.in(transistor_41_out), .out(EQ), .gate(A0_xor_B0));
  Transistor #(.\type ("n")) transistor_43 (.in(1'b0), .out(EQ), .gate(A1_xor_B1));
  Transistor #(.\type ("n")) transistor_44 (.in(1'b0), .out(EQ), .gate(A0_xor_B0));
  Transistor transistor_45 ();  // open: in, out, gate

  // Notes on the sheet:
  //   P type
  //   N type
endmodule

module schema_in_gates (
  input  A2,
  input  B2,
  input  A1,
  input  B1,
  input  A0,
  input  B0,
  output GT,
  output EQ,
  output LT
);

  wire nand_1_out, nand_2_out, nor_1_out, nor_2_out, nor_3_out, nor_4_out, nor_5_out, nor_6_out, not_1_out,
       not_2_out, not_3_out, not_4_out, not_5_out, not_6_out;

  not not_1 (not_1_out, A2);
  not not_2 (not_2_out, B2);
  nor nor_1 (nor_1_out, B2, not_1_out);
  nor nor_2 (nor_2_out, not_2_out, A2);
  not not_3 (not_3_out, A1);
  not not_4 (not_4_out, B1);
  nor nor_3 (nor_3_out, B1, not_3_out, nor_2_out);
  nor nor_4 (nor_4_out, not_4_out, A1, nor_1_out);
  nor nor_5 (nor_5_out, nor_3_out, nor_1_out);
  nor nor_6 (nor_6_out, nor_4_out, nor_2_out);
  not not_5 (not_5_out, B0);
  not not_6 (not_6_out, A0);
  nand nand_1 (nand_1_out, not_5_out, A0, nor_6_out);
  nand nand_2 (nand_2_out, B0, not_6_out, nor_5_out);
  nand nand_3 (GT, nand_1_out, nor_5_out);
  nand nand_4 (LT, nand_2_out, nor_6_out);
  nor nor_7 (EQ, GT, LT);

  // Notes on the sheet:
  //   2
  //   2
  //   4
  //   4
  //   2
  //   2
  //   6
  //   6
  //   4
  //   4
  //   2
  //   2
  //   6
  //   6
  //   4
  //   4
  //   4
endmodule

module schema_in_FETs (
  input  A2,
  input  B2,
  input  A1,
  input  B1,
  input  A0,
  input  B0,
  output GT,
  output EQ,
  output LT
);

  wire transistor_3_out, transistor_5_out, transistor_6_out, transistor_8_out, transistor_11_out,
       transistor_12_out, transistor_15_out, transistor_17_out, transistor_18_out, transistor_20_out,
       transistor_23_out, transistor_24_out, transistor_27_out, transistor_28_out, transistor_31_out,
       transistor_32_out, transistor_33_out, transistor_36_out, transistor_39_out, transistor_41_out,
       transistor_43_out, transistor_44_out, transistor_49_out, transistor_50_out, transistor_53_out,
       transistor_54_out, transistor_59_out, transistor_62_out, transistor_64_out;

  Transistor transistor_1 ();  // open: in, out, gate
  Transistor #(.\type ("n")) transistor_2 ();  // open: in, out, gate
  // Transmission_Gate transmission_1: pin names not known
  Transistor transistor_3 (.in(1'b1), .out(transistor_3_out), .gate(A2));
  Transistor #(.\type ("n")) transistor_4 (.in(1'b0), .out(transistor_3_out), .gate(A2));
  Transistor transistor_5 (.in(1'b1), .out(transistor_5_out), .gate(B2));
  Transistor transistor_6 (.in(transistor_5_out), .out(transistor_6_out), .gate(transistor_3_out));
  Transistor #(.\type ("n")) transistor_7 (.in(1'b0), .out(transistor_6_out), .gate(transistor_3_out));
  Transistor transistor_8 (.in(1'b1), .out(transistor_8_out), .gate(B2));
  Transistor #(.\type ("n")) transistor_9 (.in(1'b0), .out(transistor_8_out), .gate(B2));
  Transistor #(.\type ("n")) transistor_10 (.in(1'b0), .out(transistor_6_out), .gate(B2));
  Transistor transistor_11 (.in(1'b1), .out(transistor_11_out), .gate(A2));
  Transistor transistor_12 (.in(transistor_11_out), .out(transistor_12_out), .gate(transistor_8_out));
  Transistor #(.\type ("n")) transistor_13 (.in(1'b0), .out(transistor_12_out), .gate(A2));
  Transistor #(.\type ("n")) transistor_14 (.in(1'b0), .out(transistor_12_out), .gate(transistor_8_out));
  Transistor transistor_15 (.in(1'b1), .out(transistor_15_out), .gate(A1));
  Transistor #(.\type ("n")) transistor_16 (.in(1'b0), .out(transistor_15_out), .gate(A1));
  Transistor #(.\type ("n")) transistor_17 (.in(1'b0), .out(transistor_17_out), .gate(transistor_12_out));
  Transistor transistor_18 (.in(1'b1), .out(transistor_18_out), .gate(B1));
  Transistor #(.\type ("n")) transistor_19 (.in(1'b0), .out(transistor_18_out), .gate(B1));
  Transistor #(.\type ("n")) transistor_20 (.in(1'b0), .out(transistor_20_out), .gate(transistor_6_out));
  Transistor #(.\type ("n")) transistor_21 (.in(1'b0), .out(transistor_17_out), .gate(B1));
  Transistor #(.\type ("n")) transistor_22 (.in(1'b0), .out(transistor_20_out), .gate(A1));
  Transistor transistor_23 (.in(1'b1), .out(transistor_23_out), .gate(transistor_15_out));
  Transistor transistor_24 (.in(transistor_23_out), .out(transistor_24_out), .gate(B1));
  Transistor transistor_25 (.in(transistor_24_out), .out(transistor_17_out), .gate(transistor_12_out));
  Transistor #(.\type ("n")) transistor_26 (.in(1'b0), .out(transistor_17_out), .gate(transistor_15_out));
  Transistor transistor_27 (.in(1'b1), .out(transistor_27_out), .gate(transistor_18_out));
  Transistor transistor_28 (.in(transistor_27_out), .out(transistor_28_out), .gate(A1));
  Transistor transistor_29 (.in(transistor_28_out), .out(transistor_20_out), .gate(transistor_6_out));
  Transistor #(.\type ("n")) transistor_30 (.in(1'b0), .out(transistor_20_out), .gate(transistor_18_out));
  Transistor #(.\type ("n")) transistor_31 (.in(1'b0), .out(transistor_31_out), .gate(transistor_17_out));
  Transistor #(.\type ("n")) transistor_32 (.in(1'b0), .out(transistor_32_out), .gate(transistor_20_out));
  Transistor transistor_33 (.in(1'b1), .out(transistor_33_out), .gate(transistor_17_out));
  Transistor transistor_34 (.in(transistor_33_out), .out(transistor_31_out), .gate(transistor_6_out));
  Transistor #(.\type ("n")) transistor_35 (.in(1'b0), .out(transistor_31_out), .gate(transistor_6_out));
  Transistor transistor_36 (.in(1'b1), .out(transistor_36_out), .gate(transistor_20_out));
  Transistor transistor_37 (.in(transistor_36_out), .out(transistor_32_out), .gate(transistor_12_out));
  Transistor #(.\type ("n")) transistor_38 (.in(1'b0), .out(transistor_32_out), .gate(transistor_12_out));
  Transistor transistor_39 (.in(1'b1), .out(transistor_39_out), .gate(B0));
  Transistor #(.\type ("n")) transistor_40 (.in(1'b0), .out(transistor_39_out), .gate(B0));
  Transistor transistor_41 (.in(1'b1), .out(transistor_41_out), .gate(A0));
  Transistor #(.\type ("n")) transistor_42 (.in(1'b0), .out(transistor_41_out), .gate(A0));
  Transistor transistor_43 (.in(1'b1), .out(transistor_43_out), .gate(transistor_41_out));
  Transistor transistor_44 (.in(1'b1), .out(transistor_44_out), .gate(transistor_39_out));
  Transistor transistor_45 (.in(1'b1), .out(transistor_44_out), .gate(A0));
  Transistor transistor_46 (.in(1'b1), .out(transistor_43_out), .gate(transistor_31_out));
  Transistor transistor_47 (.in(1'b1), .out(transistor_43_out), .gate(B0));
  Transistor #(.\type ("n")) transistor_48 (.in(transistor_49_out), .out(transistor_43_out), .gate(B0));
  Transistor #(.\type ("n")) transistor_49 (.in(transistor_50_out), .out(transistor_49_out), .gate(transistor_31_out));
  Transistor #(.\type ("n")) transistor_50 (.in(1'b0), .out(transistor_50_out), .gate(transistor_41_out));
  Transistor transistor_51 (.in(1'b1), .out(transistor_44_out), .gate(transistor_32_out));
  Transistor #(.\type ("n")) transistor_52 (.in(transistor_53_out), .out(transistor_44_out), .gate(transistor_32_out));
  Transistor #(.\type ("n")) transistor_53 (.in(transistor_54_out), .out(transistor_53_out), .gate(transistor_39_out));
  Transistor #(.\type ("n")) transistor_54 (.in(1'b0), .out(transistor_54_out), .gate(A0));
  Transistor transistor_55 (.in(1'b1), .out(LT), .gate(transistor_43_out));
  Transistor transistor_56 (.in(1'b1), .out(GT), .gate(transistor_31_out));
  Transistor transistor_57 (.in(1'b1), .out(GT), .gate(transistor_44_out));
  Transistor #(.\type ("n")) transistor_58 (.in(transistor_59_out), .out(GT), .gate(transistor_31_out));
  Transistor #(.\type ("n")) transistor_59 (.in(1'b0), .out(transistor_59_out), .gate(transistor_44_out));
  Transistor transistor_60 (.in(1'b1), .out(LT), .gate(transistor_32_out));
  Transistor #(.\type ("n")) transistor_61 (.in(transistor_62_out), .out(LT), .gate(transistor_32_out));
  Transistor #(.\type ("n")) transistor_62 (.in(1'b0), .out(transistor_62_out), .gate(transistor_43_out));
  Transistor #(.\type ("n")) transistor_63 (.in(1'b0), .out(EQ), .gate(LT));
  Transistor transistor_64 (.in(1'b1), .out(transistor_64_out), .gate(LT));
  Transistor transistor_65 (.in(transistor_64_out), .out(EQ), .gate(GT));
  Transistor #(.\type ("n")) transistor_66 (.in(1'b0), .out(EQ), .gate(GT));

  // Notes on the sheet:
  //   P type
  //   N type
endmodule
